// Logisim project IT012_Lab02_25520149.circ as structural Verilog: 9 circuits, main circuit FA
module FA (
  input  A,
  input  B,
  input  Cin,
  output S,
  output Cout
);

  wire and_1_out, and_2_out, xor_1_out;

  xor xor_1 (xor_1_out, A, B);
  and and_1 (and_1_out, xor_1_out, Cin);
  and and_2 (and_2_out, B, A);
  xor xor_2 (S, xor_1_out, Cin);
  or or_1 (Cout, and_1_out, and_2_out);
endmodule

module ADDSUB4 (
  input  [3:0] A,
  input  [3:0] B,
  input  SUB,
  output [3:0] S,
  output Cout
);

  wire fa_1_cout, fa_2_cout, fa_3_cout, xor_1_out, xor_2_out, xor_3_out, xor_4_out;

  xor xor_1 (xor_1_out, B[0], SUB);
  xor xor_2 (xor_2_out, B[1], SUB);
  xor xor_3 (xor_3_out, B[2], SUB);
  xor xor_4 (xor_4_out, B[3], SUB);
  FA fa_1 (.A(A[0]), .B(xor_1_out), .Cin(SUB), .S(S[0]), .Cout(fa_1_cout));
  // Probe on fa_1_cout
  FA fa_2 (.A(A[1]), .B(xor_2_out), .Cin(fa_1_cout), .S(S[1]), .Cout(fa_2_cout));
  FA fa_3 (.A(A[2]), .B(xor_3_out), .Cin(fa_2_cout), .S(S[2]), .Cout(fa_3_cout));
  FA fa_4 (.A(A[3]), .B(xor_4_out), .Cin(fa_3_cout), .S(S[3]), .Cout(Cout));
  // Probe on fa_2_cout
  // Probe on fa_3_cout
endmodule

module ALU8 (
  input  [2:0] OP,
  input  [7:0] A,
  input  [7:0] B,
  output [7:0] R,
  output Z,
  output LT
);

  wire [7:0] adder_1_out, adder_2_out, and_1_out, multiplexer_1_out, multiplexer_2_out, not_1_out, or_1_out,
       subtractor_1_out, subtractor_2_out, xor_1_out;

  LT lt_1 (.A7(A[7]), .B7(B[7]), .R7(R[7]), .LT(LT));
  Adder adder_1 (.a(A), .b(B), .out(adder_1_out));  // open: cin, cout
  Adder adder_2 (.a(A), .b(8'h1), .out(adder_2_out));  // open: cin, cout
  Subtractor subtractor_1 (.a(A), .b(B), .out(subtractor_1_out));  // open: bin, bout
  Subtractor subtractor_2 (.a(A), .b(8'h1), .out(subtractor_2_out));  // open: bin, bout
  assign and_1_out = A & B;  // AND_Gate and_1, 8 bits wide
  assign or_1_out = A | B;  // OR_Gate or_1, 8 bits wide
  assign not_1_out = ~A;  // NOT_Gate not_1, 8 bits wide
  assign xor_1_out = A ^ B;  // XOR_Gate xor_1, 8 bits wide
  Multiplexer #(.select(2), .width(8)) multiplexer_1 (
    .in0(adder_1_out), .in1(adder_2_out), .in2(subtractor_1_out), .in3(subtractor_2_out),
    .out(multiplexer_1_out), .sel(OP[1:0]));  // open: en
  Multiplexer #(.select(2), .width(8)) multiplexer_2 (
    .in0(and_1_out), .in1(or_1_out), .in2(not_1_out), .in3(xor_1_out), .out(multiplexer_2_out), .sel(OP[1:0]));  // open: en
  Multiplexer #(.width(8)) multiplexer_3 (
    .in0(multiplexer_1_out), .in1(multiplexer_2_out), .out(R), .sel(OP[2]));  // open: en
  nor nor_1 (Z, R[7], R[6], R[5], R[4], R[3], R[2], R[1], R[0]);
endmodule

module LT (
  input  A7,
  input  B7,
  input  R7,
  output LT
);

  wire and_1_out, and_2_out, and_3_out, not_1_out;

  not not_1 (not_1_out, B7);
  and and_1 (and_1_out, A7, not_1_out);
  and and_2 (and_2_out, not_1_out, R7);
  and and_3 (and_3_out, A7, R7);
  or or_1 (LT, and_1_out, and_2_out, and_3_out);
endmodule

module TN3 (
  input  CLK,
  input  D,
  input  D_2,
  input  CLK_2,
  output Q1,
  output Q2,
  output Q3,
  output Q1_dff,
  output Q1_latch,
  output Q2_dff,
  output Q2_latch
);

  wire Master_q, not_1_out;

  DLATCH dlatch_1 (.E(CLK), .Q(Q1), .D(D));
  DLATCH Latch_1 (.E(CLK_2), .Q(Q1_latch), .D(D_2));
  DLATCH Latch_2 (.E(CLK_2), .Q(Q2_latch), .D(Q1_latch));
  D_Flip_Flop d_ff_1 (.clk(CLK), .D(D), .Q(Q2));  // open: Qn, preset, en, reset
  D_Flip_Flop DFF_1 (.clk(CLK_2), .D(D_2), .Q(Q1_dff));  // open: Qn, preset, en, reset
  D_Flip_Flop DFF_2 (.clk(CLK_2), .D(Q1_dff), .Q(Q2_dff));  // open: Qn, preset, en, reset
  not not_1 (not_1_out, CLK);
  DLATCH Master (.E(not_1_out), .Q(Master_q), .D(D));
  DLATCH Slave (.E(CLK), .Q(Q3), .D(Master_q));
endmodule

module DLATCH (
  input  E,
  input  D,
  output Q
);

  Multiplexer multiplexer_1 (.in0(Q), .in1(D), .out(Q), .sel(E));  // open: en
endmodule

module REGFILE (
  input  [7:0] R0,
  input  [7:0] QB,
  input  [7:0] R1,
  input  [1:0] RB,
  input  [7:0] R2,
  input  [7:0] R3,
  input  [7:0] QA,
  input  [1:0] RA,
  input  [7:0] DIN,
  input  CLK,
  input  [1:0] RD,
  input  WE
);

  wire and_1_out, and_2_out, and_3_out, and_4_out, decoder_1_out0, decoder_1_out1, decoder_1_out2,
       decoder_1_out3, undriven, undriven_2;

  Decoder #(.select(2), .enable("false")) decoder_1 (
    .out0(decoder_1_out0), .out1(decoder_1_out1), .out2(decoder_1_out2), .out3(decoder_1_out3), .sel(RD));
  Register register_1 (.clr(DIN[0]));  // open: D, en, Q, clk
  and and_1 (and_1_out, decoder_1_out0, WE, undriven);
  and and_2 (and_2_out, undriven, WE, decoder_1_out1);
  and and_3 (and_3_out, decoder_1_out2, WE, undriven_2);
  and and_4 (and_4_out, undriven_2, WE, decoder_1_out3);
  Register register_2 (.D(R0), .en(R0[0]), .clr(DIN[0]));  // open: Q, clk
  Register register_3 (.D(R1), .en(R1[0]), .clr(DIN[0]));  // open: Q, clk
  Register register_4 (.clk(DIN[0]));  // open: D, en, Q, clr
  Multiplexer #(.select(2), .width(8)) multiplexer_1 (
    .in0(R0), .in1(R1), .in2(R2), .in3(R3), .out(QB), .sel(RB));  // open: en
  Multiplexer #(.select(2), .width(8)) multiplexer_2 (
    .in0(R0), .in1(R1), .in2(R2), .in3(R3), .out(QA), .sel(RA));  // open: en
  // Pins of 1 and 8 bits meet at R0
  // Pins of 1 and 8 bits meet at R1
  // Pins of 1 and 8 bits meet at DIN
endmodule

module DATAPATH (
  input  [1:0] RB,
  input  [7:0] R0,
  input  [1:0] RA,
  input  [7:0] R1,
  input  [7:0] R2,
  input  CLK,
  input  [7:0] R3,
  input  [1:0] RD,
  input  Z,
  input  WE,
  input  [2:0] OP,
  input  [7:0] R,
  input  [7:0] IMM,
  input  SRC
);

  wire [7:0] multiplexer_1_out;

  Multiplexer #(.width(8)) multiplexer_1 (.in0(R), .in1(IMM), .out(multiplexer_1_out), .sel(SRC));  // open: en
endmodule

module DFF_MS (
  input  D,
  input  Q3,
  input  CLK
);

  wire not_1_out;

  not not_1 (not_1_out, CLK);
endmodule
